// Logisim project 11-10-2023.circ as structural Verilog: 1 circuit, main circuit main
module main (
);

  wire CLK;
  wire [2:0] d_ff_3_q;
  wire [3:0] rom_1_data;

  ROM #(.addrWidth(3), .dataWidth(4)) rom_1 (.addr(d_ff_3_q), .data(rom_1_data));  // open: sel
  Clock clock_1 (.out(CLK));
  LED led_1 (.in(rom_1_data[0]));
  D_Flip_Flop d_ff_1 (.clk(CLK), .D(rom_1_data[3]), .Q(d_ff_3_q[2]));  // open: Qn, preset, en, reset
  D_Flip_Flop d_ff_2 (.clk(CLK), .D(rom_1_data[2]), .Q(d_ff_3_q[1]));  // open: Qn, preset, en, reset
  D_Flip_Flop d_ff_3 (.clk(CLK), .D(rom_1_data[1]), .Q(d_ff_3_q[0]));  // open: Qn, preset, en, reset

  // Notes on the sheet:
  //   contents of rom_1 (hex, n*v repeats v):
  //   2 5 7 9 a d e 1
endmodule
