// Logisim project Diseño Multiplicador con multiplexer  (1).circ as structural Verilog: 1 circuit, main circuit main
module main (
  input  in_1,
  input  in_2,
  input  in_3,
  input  in_4,
  input  Inicio,
  input  B0,
  input  B1,
  input  B2,
  input  in_9,
  input  B3,
  output [7:0] out_11
);

  wire clock_1_out;
  wire [0:0] multiplexer_1_out;
  wire [3:0] d_ff_1_q;
  wire [7:0] adder_1_out, rom_1_data, shift_register_1_q0;

  Multiplexer #(.select(4)) multiplexer_1 (
    .in0(Inicio), .in1(B0), .in2(1'b0), .in3(B1), .in4(1'b0), .in5(B2), .in6(1'b0), .in7(B3), .in8(1'b0),
    .in9(1'b0), .in10(1'b0), .in11(1'b0), .in12(1'b0), .in13(1'b0), .in14(1'b0), .in15(1'b0),
    .out(multiplexer_1_out[0]), .sel(d_ff_1_q), .en(1'b1));
  ROM #(.addrWidth(5)) rom_1 (.addr({d_ff_1_q, multiplexer_1_out[0]}), .data(rom_1_data));  // open: sel
  Clock clock_1 (.out(clock_1_out));
  D_Flip_Flop d_ff_1 (.clk(clock_1_out), .D(rom_1_data[4]), .Q(d_ff_1_q[0]));  // open: Qn, preset, en, reset
  D_Flip_Flop d_ff_2 (.clk(clock_1_out), .D(rom_1_data[5]), .Q(d_ff_1_q[1]));  // open: Qn, preset, en, reset
  D_Flip_Flop d_ff_3 (.clk(clock_1_out), .D(rom_1_data[6]), .Q(d_ff_1_q[2]));  // open: Qn, preset, en, reset
  D_Flip_Flop d_ff_4 (.clk(clock_1_out), .D(rom_1_data[7]), .Q(d_ff_1_q[3]));  // open: Qn, preset, en, reset
  Shift_Register shift_register_1 (
    .shift(rom_1_data[2]), .in(in_9), .clk(clock_1_out), .load(rom_1_data[3]), .d0(in_4),
    .q0(shift_register_1_q0[0]), .d1(in_3), .q1(shift_register_1_q0[1]), .d2(in_2),
    .q2(shift_register_1_q0[2]), .d3(in_1), .q3(shift_register_1_q0[3]), .d4(1'b0),
    .q4(shift_register_1_q0[4]), .d5(1'b0), .q5(shift_register_1_q0[5]), .d6(1'b0),
    .q6(shift_register_1_q0[6]), .d7(1'b0), .q7(shift_register_1_q0[7]));  // open: out, clr
  Adder adder_1 (.a(shift_register_1_q0), .b(out_11), .out(adder_1_out));  // open: cin, cout
  Register register_1 (.D(adder_1_out), .Q(out_11), .clk(rom_1_data[1]), .clr(rom_1_data[0]));  // open: en

  // Notes on the sheet:
  //   contents of rom_1 (hex, n*v repeats v):
  //   0 10 39 29 32 32 54 44 52 52 74 64 72 72 94 84 92 92 4 4
endmodule
