// Logisim project ElevadorJyR.circ as structural Verilog: 1 circuit, main circuit main
module main (
  output [1:0] out_1,
  output out_2,
  output out_3
);

  wire B0S, B1B, B1S, B2B, B2S, B3B, button_1_out, button_2_out, button_3_out, button_4_out, button_5_out,
       button_6_out, button_7_out, button_8_out, button_9_out, button_10_out, CLK, d_ff_11_qn, d_ff_12_q,
       d_ff_14_q, d_ff_15_q, decoder_1_out1, decoder_1_out2, decoder_1_out3, decoder_2_out0, decoder_2_out1,
       decoder_2_out2, decoder_2_out3, decoder_3_out0, decoder_3_out1, decoder_3_out2, multiplexer_1_out,
       multiplexer_2_out, multiplexer_3_out, not_1_out, not_2_out, or_1_out, or_2_out, or_3_out, or_4_out,
       or_5_out, P0, P1, P2, P3;
  wire [1:0] Elevador;
  wire [4:0] rom_1_data;
  wire [6:0] comparator_1_eq;

  Decoder #(.select(2)) decoder_1 (
    .out1(decoder_1_out1), .out2(decoder_1_out2), .out3(decoder_1_out3), .sel(Elevador), .en(d_ff_15_q));  // open: out0
  Decoder #(.select(2)) decoder_2 (
    .out0(decoder_2_out0), .out1(decoder_2_out1), .out2(decoder_2_out2), .out3(decoder_2_out3),
    .sel(Elevador), .en(or_1_out));
  or or_1 (or_1_out, d_ff_15_q, d_ff_14_q);
  Decoder #(.select(2)) decoder_3 (
    .out0(decoder_3_out0), .out1(decoder_3_out1), .out2(decoder_3_out2), .sel(Elevador), .en(d_ff_14_q));  // open: out3
  Button button_1 (.out(button_1_out));
  Button button_2 (.out(button_2_out));
  Button button_3 (.out(button_3_out));
  Button button_4 (.out(button_4_out));
  Button button_5 (.out(button_5_out));
  Button button_6 (.out(button_6_out));
  Button button_7 (.out(button_7_out));
  Button button_8 (.out(button_8_out));
  Button button_9 (.out(button_9_out));
  Button button_10 (.out(button_10_out));
  D_Flip_Flop d_ff_1 (.D(1'b1), .clk(button_1_out), .Q(B0S), .reset(decoder_3_out0));  // open: Qn, preset
  D_Flip_Flop d_ff_2 (.D(1'b1), .clk(button_2_out), .Q(P0), .reset(decoder_2_out0));  // open: Qn, preset
  D_Flip_Flop d_ff_3 (.D(1'b1), .clk(button_3_out), .Q(B1S), .reset(decoder_3_out1));  // open: Qn, preset
  D_Flip_Flop d_ff_4 (.D(1'b1), .clk(button_4_out), .Q(P1), .reset(decoder_2_out1));  // open: Qn, preset
  D_Flip_Flop d_ff_5 (.D(1'b1), .clk(button_5_out), .Q(B1B), .reset(decoder_1_out1));  // open: Qn, preset
  D_Flip_Flop d_ff_6 (.D(1'b1), .clk(button_6_out), .Q(P2), .reset(decoder_2_out2));  // open: Qn, preset
  D_Flip_Flop d_ff_7 (.D(1'b1), .clk(button_7_out), .Q(B2B), .reset(decoder_1_out2));  // open: Qn, preset
  D_Flip_Flop d_ff_8 (.D(1'b1), .clk(button_8_out), .Q(B2S), .reset(decoder_3_out2));  // open: Qn, preset
  D_Flip_Flop d_ff_9 (.D(1'b1), .clk(button_9_out), .Q(P3), .reset(decoder_2_out3));  // open: Qn, preset
  D_Flip_Flop d_ff_10 (.D(1'b1), .clk(button_10_out), .Q(B3B), .reset(decoder_1_out3));  // open: Qn, preset
  or or_2 (or_2_out, B0S, P0);
  or or_3 (or_3_out, B1S, P1, B1B);
  or or_4 (or_4_out, P2, B2B, B2S);
  or or_5 (or_5_out, P3, B3B);
  Multiplexer #(.enable("true"), .select(2)) multiplexer_1 (
    .in0(or_2_out), .in1(or_3_out), .in2(or_4_out), .in3(or_5_out), .out(multiplexer_1_out), .sel(out_1));  // open: en
  Clock clock_1 (.out(CLK));
  not not_1 (not_1_out, multiplexer_1_out);
  Counter #(.max('h3), .width(2)) counter_1 (
    .load(1'b0), .up(1'b1), .count(not_1_out), .clk(CLK), .Q(out_1));  // open: clr, D, carry
  or or_6 (comparator_1_eq[6], or_2_out, or_3_out, or_4_out, or_5_out);
  Multiplexer #(.enable("true"), .select(2)) multiplexer_2 (
    .in0(B0S), .in1(B1S), .in2(B2S), .in3(1'b0), .out(multiplexer_2_out), .sel(Elevador));  // open: en
  Multiplexer #(.enable("true"), .select(2)) multiplexer_3 (
    .in0(1'b0), .in1(B1B), .in2(B2B), .in3(B3B), .out(multiplexer_3_out), .sel(Elevador));  // open: en
  Multiplexer #(.enable("true"), .select(2)) multiplexer_4 (
    .in0(P0), .in1(P1), .in2(P2), .in3(P3), .out(out_3), .sel(Elevador));  // open: en
  or or_7 (comparator_1_eq[4], multiplexer_2_out, out_3);
  or or_8 (comparator_1_eq[3], multiplexer_3_out, out_3);
  Comparator #(.mode("unsigned"), .width(2)) comparator_1 (
    .a(out_1), .b(Elevador), .gt(comparator_1_eq[2]), .eq(comparator_1_eq[0]), .lt(comparator_1_eq[1]));
  ROM #(.addrWidth(7), .dataWidth(5)) rom_1 (.addr(comparator_1_eq), .data(rom_1_data));
  not not_2 (not_2_out, CLK);
  D_Flip_Flop d_ff_11 (
    .D(rom_1_data[4]), .clk(not_2_out), .Q(comparator_1_eq[5]), .Qn(d_ff_11_qn));  // open: preset, reset
  D_Flip_Flop d_ff_12 (.D(rom_1_data[3]), .clk(not_2_out), .Q(d_ff_12_q));  // open: Qn, preset, reset
  D_Flip_Flop d_ff_13 (.D(rom_1_data[2]), .clk(not_2_out), .Q(out_2));  // open: Qn, preset, reset
  D_Flip_Flop d_ff_14 (.D(rom_1_data[1]), .clk(not_2_out), .Q(d_ff_14_q));  // open: Qn, preset, reset
  D_Flip_Flop d_ff_15 (.D(rom_1_data[0]), .clk(not_2_out), .Q(d_ff_15_q));  // open: Qn, preset, reset
  Counter #(.max('h3), .width(2)) counter_2 (
    .up(comparator_1_eq[5]), .count(d_ff_12_q), .clk(CLK), .Q(Elevador));  // open: clr, load, D, carry
  Hex_Digit_Display hex_digit_display_1 (.value({2'b00, Elevador}));  // open: dp

  // Other names for the same wires on the sheet: Pll[1:0] = out_1

  // Notes on the sheet:
  //   B0S
  //   0
  //   B1S
  //   1
  //   B1B
  //   2
  //   B2B
  //   B2S
  //   3
  //   B3B
  //   ¿Hay llamada?
  //   S/B
  //   mover
  //   llamada
  //   piso llamado
  //   ¿para donde me muevo?
  //   bajar
  //   ¿Hay llamadas para arriba?
  //   ¿en donde abro la puerta?
  //   Atiende pisos de subida
  //   ¿Hay llamadas para abajo?
  //   Atiende pisos de bajada
  //   subir
  //   mismo piso
  //   contents of rom_1 (hex, n*v repeats v):
  //   65*0 7 8 0 18 4*0 7 5 6*0 7 8 0 16 4*0 7 5 0 17 4*0 17 8 0 18 4*0 17 5 0 18 4*0 17 0 0 16 4*0 17 7 0
  //   16
endmodule
