// Logisim project ElevadorPlanta (1).circ as structural Verilog: 1 circuit, main circuit main
module main (
  input  in_1,
  input  in_2,
  input  borrarS,
  input  borrarB,
  output [1:0] out_5,
  output subir,
  output Hay_llamada,
  output out_8,
  output bajar,
  output out_10,
  output out_11,
  output out_12,
  output out_13,
  output out_14
);

  wire B0S, B1B, B1S, B2B, B2S, B3B, button_1_out, button_2_out, button_3_out, button_4_out, button_5_out,
       button_6_out, button_7_out, button_8_out, button_9_out, button_10_out, CLK, decoder_1_out1,
       decoder_1_out2, decoder_1_out3, decoder_2_out0, decoder_2_out1, decoder_2_out2, decoder_2_out3,
       decoder_3_out0, decoder_3_out1, decoder_3_out2, multiplexer_1_out, multiplexer_2_out,
       multiplexer_3_out, not_1_out, or_1_out, or_2_out, or_3_out, or_4_out, or_5_out, P0, P1, P2, P3;
  wire [1:0] Elevador;

  Decoder #(.select(2)) decoder_1 (
    .out1(decoder_1_out1), .out2(decoder_1_out2), .out3(decoder_1_out3), .sel(Elevador), .en(borrarB));  // open: out0
  Decoder #(.select(2)) decoder_2 (
    .out0(decoder_2_out0), .out1(decoder_2_out1), .out2(decoder_2_out2), .out3(decoder_2_out3),
    .sel(Elevador), .en(or_1_out));
  or or_1 (or_1_out, borrarB, borrarS);
  Decoder #(.select(2)) decoder_3 (
    .out0(decoder_3_out0), .out1(decoder_3_out1), .out2(decoder_3_out2), .sel(Elevador), .en(borrarS));  // open: out3
  Button button_1 (.out(button_1_out));
  Button button_2 (.out(button_2_out));
  Button button_3 (.out(button_3_out));
  Button button_4 (.out(button_4_out));
  Button button_5 (.out(button_5_out));
  Button button_6 (.out(button_6_out));
  Button button_7 (.out(button_7_out));
  Button button_8 (.out(button_8_out));
  Button button_9 (.out(button_9_out));
  Button button_10 (.out(button_10_out));
  D_Flip_Flop d_ff_1 (.D(1'b1), .clk(button_1_out), .Q(B0S), .reset(decoder_3_out0));  // open: Qn, preset
  D_Flip_Flop d_ff_2 (.D(1'b1), .clk(button_2_out), .Q(P0), .reset(decoder_2_out0));  // open: Qn, preset
  D_Flip_Flop d_ff_3 (.D(1'b1), .clk(button_3_out), .Q(B1S), .reset(decoder_3_out1));  // open: Qn, preset
  D_Flip_Flop d_ff_4 (.D(1'b1), .clk(button_4_out), .Q(P1), .reset(decoder_2_out1));  // open: Qn, preset
  D_Flip_Flop d_ff_5 (.D(1'b1), .clk(button_5_out), .Q(B1B), .reset(decoder_1_out1));  // open: Qn, preset
  D_Flip_Flop d_ff_6 (.D(1'b1), .clk(button_6_out), .Q(P2), .reset(decoder_2_out2));  // open: Qn, preset
  D_Flip_Flop d_ff_7 (.D(1'b1), .clk(button_7_out), .Q(B2B), .reset(decoder_1_out2));  // open: Qn, preset
  D_Flip_Flop d_ff_8 (.D(1'b1), .clk(button_8_out), .Q(B2S), .reset(decoder_3_out2));  // open: Qn, preset
  D_Flip_Flop d_ff_9 (.D(1'b1), .clk(button_9_out), .Q(P3), .reset(decoder_2_out3));  // open: Qn, preset
  D_Flip_Flop d_ff_10 (.D(1'b1), .clk(button_10_out), .Q(B3B), .reset(decoder_1_out3));  // open: Qn, preset
  or or_2 (or_2_out, B0S, P0);
  or or_3 (or_3_out, B1S, P1, B1B);
  or or_4 (or_4_out, P2, B2B, B2S);
  or or_5 (or_5_out, P3, B3B);
  ROM rom_1 ();  // open: addr, data
  Multiplexer #(.select(2)) multiplexer_1 (
    .in0(or_2_out), .in1(or_3_out), .in2(or_4_out), .in3(or_5_out), .out(multiplexer_1_out), .sel(out_5));
  Clock clock_1 (.out(CLK));
  not not_1 (not_1_out, multiplexer_1_out);
  Counter #(.max('h3), .width(2)) counter_1 (
    .load(1'b0), .up(1'b1), .count(not_1_out), .clk(CLK), .Q(out_5));  // open: clr, D, carry
  or or_6 (Hay_llamada, or_2_out, or_3_out, or_4_out, or_5_out);
  Multiplexer #(.select(2)) multiplexer_2 (
    .in0(B0S), .in1(B1S), .in2(B2S), .in3(1'b0), .out(multiplexer_2_out), .sel(Elevador));
  Multiplexer #(.select(2)) multiplexer_3 (
    .in0(1'b0), .in1(B1B), .in2(B2B), .in3(B3B), .out(multiplexer_3_out), .sel(Elevador));
  Multiplexer #(.select(2)) multiplexer_4 (.in0(P0), .in1(P1), .in2(P2), .in3(P3), .out(out_14), .sel(Elevador));
  or or_7 (out_10, B2S, B1S, B0S);
  or or_8 (out_11, multiplexer_2_out, out_14);
  or or_9 (out_13, multiplexer_3_out, out_14);
  Counter #(.max('h3), .width(2)) counter_2 (
    .up(in_1), .count(in_2), .clk(CLK), .Q(Elevador));  // open: clr, load, D, carry
  or or_10 (out_12, B1B, B2B, B3B);
  Comparator #(.mode("unsigned"), .width(2)) comparator_1 (.a(out_5), .b(Elevador), .gt(subir), .eq(out_8), .lt(bajar));
  Hex_Digit_Display hex_digit_display_1 (.value({2'b00, Elevador}));  // open: dp

  // Other names for the same wires on the sheet: Pll[1:0] = out_5

  // Notes on the sheet:
  //   B0S
  //   0
  //   B1S
  //   1
  //   B1B
  //   2
  //   B2B
  //   B2S
  //   3
  //   B3B
  //   S/B
  //   mover
  //   llamada
  //   piso llamado
  //   ¿en donde abro la puerta?
  //   ¿para donde me muevo?
  //   ¿Hay llamadas para arriba?
  //   Atiende pisos de subida
  //   ¿Hay llamadas para abajo?
  //   Atiende pisos de bajada
  //   mismo piso
endmodule
