// Logisim project Multiplicador con Registros-1 (1).circ as structural Verilog: 1 circuit, main circuit main
module main (
  input  _4,
  input  _3,
  input  _2,
  input  _1,
  input  L,
  input  in_6,
  input  in_7,
  input  msb,
  input  _4_2,
  input  _3_2,
  input  _2_2,
  input  _1_2,
  input  in_13,
  input  in_14,
  input  in_15,
  input  B0,
  input  B1,
  input  clear,
  input  B2,
  input  B3,
  input  B0_2,
  input  B1_2,
  input  B2_2,
  input  B3_2,
  output [7:0] Suma,
  output [7:0] Suma_2,
  output [7:0] Suma_3,
  output [7:0] Resultado,
  output [7:0] Resultado_2,
  output [7:0] Resultado_3
);

  wire button_2_out, clock_1_out, clock_2_out, clock_3_out;
  wire [4:0] multiplexer_1_out;
  wire [7:0] rom_1_data, rom_2_data, shift_register_1_q0, shift_register_2_q0, shift_register_3_q0;
  wire [8:0] button_1_out;

  Button button_1 (.out(button_1_out[0]));
  Clock clock_1 (.out(clock_1_out));
  Shift_Register shift_register_1 (
    .shift(rom_1_data[3]), .in(1'b0), .clk(clock_1_out), .load(rom_1_data[2]), .d0(_4_2),
    .q0(shift_register_1_q0[0]), .d1(_3_2), .q1(shift_register_1_q0[1]), .d2(_2_2),
    .q2(shift_register_1_q0[2]), .d3(_1_2), .q3(shift_register_1_q0[3]), .d4(1'b0),
    .q4(shift_register_1_q0[4]), .d5(1'b0), .q5(shift_register_1_q0[5]), .d6(1'b0),
    .q6(shift_register_1_q0[6]), .d7(1'b0), .q7(shift_register_1_q0[7]));  // open: out, clr
  Register register_1 (.D(Suma_3), .Q(Resultado_3), .clk(rom_1_data[0]), .clr(rom_1_data[1]));  // open: en
  ROM #(.addrWidth(9)) rom_1 (
    .addr({button_1_out[8:5], B3_2, B2_2, B1_2, B0_2, button_1_out[0]}), .data(rom_1_data));  // open: sel
  Adder adder_1 (.a(shift_register_1_q0), .b(Resultado_3), .out(Suma_3));  // open: cin, cout
  Register #(.width(4)) register_2 (.D(rom_1_data[7:4]), .Q(button_1_out[8:5]), .clk(clock_1_out));  // open: en, clr
  Clock clock_2 (.out(clock_2_out));
  Shift_Register shift_register_2 (
    .shift(in_14), .in(1'b0), .clk(clock_2_out), .load(in_13), .d0(L), .q0(shift_register_2_q0[0]),
    .d1(in_6), .q1(shift_register_2_q0[1]), .d2(in_7), .q2(shift_register_2_q0[2]), .d3(msb),
    .q3(shift_register_2_q0[3]), .d4(1'b0), .q4(shift_register_2_q0[4]), .d5(1'b0),
    .q5(shift_register_2_q0[5]), .d6(1'b0), .q6(shift_register_2_q0[6]), .d7(1'b0),
    .q7(shift_register_2_q0[7]));  // open: out, clr
  Register register_3 (.D(Suma_2), .Q(Resultado_2), .clk(in_15), .clr(clear));  // open: en
  Adder adder_2 (.a(shift_register_2_q0), .b(Resultado_2), .out(Suma_2));  // open: cin, cout
  Button button_2 (.out(button_2_out));
  Multiplexer #(.select(4)) multiplexer_1 (
    .in0(button_2_out), .in1(B0), .in2(1'b0), .in3(B1), .in4(1'b0), .in5(B2), .in6(1'b0), .in7(B3),
    .in8(1'b0), .in9(1'b0), .in10(1'b0), .in11(1'b0), .in12(1'b0), .in13(1'b0), .in14(1'b0), .in15(1'b0),
    .out(multiplexer_1_out[0]), .sel(multiplexer_1_out[4:1]));  // open: en
  Clock clock_3 (.out(clock_3_out));
  Shift_Register shift_register_3 (
    .shift(rom_2_data[3]), .in(1'b0), .clk(clock_3_out), .load(rom_2_data[2]), .d0(_4),
    .q0(shift_register_3_q0[0]), .d1(_3), .q1(shift_register_3_q0[1]), .d2(_2), .q2(shift_register_3_q0[2]),
    .d3(_1), .q3(shift_register_3_q0[3]), .d4(1'b0), .q4(shift_register_3_q0[4]), .d5(1'b0),
    .q5(shift_register_3_q0[5]), .d6(1'b0), .q6(shift_register_3_q0[6]), .d7(1'b0),
    .q7(shift_register_3_q0[7]));  // open: out, clr
  Register register_4 (.D(Suma), .Q(Resultado), .clk(rom_2_data[1]), .clr(rom_2_data[0]));  // open: en
  ROM #(.addrWidth(5)) rom_2 (.addr(multiplexer_1_out), .data(rom_2_data));  // open: sel
  Adder adder_3 (.a(shift_register_3_q0), .b(Resultado), .out(Suma));  // open: cin, cout
  Register #(.width(4)) register_5 (
    .D(rom_2_data[7:4]), .Q(multiplexer_1_out[4:1]), .clk(clock_3_out));  // open: en, clr

  // Notes on the sheet:
  //   I
  //   4
  //   3
  //   2
  //   1
  //   Isb
  //   L
  //   S
  //   msb
  //   guardar
  //   registro de resultados
  //   clear
  //   contents of rom_1 (hex, n*v repeats v):
  //   0 10 0 10 0 10 0 10 0 10 0 10 0 10 0 10 0 10 0 10 0 10 0 10 0 10 0 10 0 10 0 10 36 36 26 26 36 36 26
  //   26 36 36 26 26 36 36 26 26 36 36 26 26 36 36 26 26 36 36 26 26 36 36 26 26 32*31 4*58 4*48 4*58 4*48
  //   4*58 4*48 4*58 4*48 32*51 8*78 8*68 8*78 8*68 32*71 16*98 16*88 32*91 32*8
  //   1011
  //   1010
  //   guardar
  //   Isb
  //   S
  //   registro de resultados
  //   1010
  //   1011
  //   4
  //   3
  //   2
  //   1
  //   I
  //   Siempre en 1
  //   En armado a 0
  //   S
  //   Isb
  //   L
  //   msb
  //   guardar
  //   registro de resultados
  //   clear
  //   contents of rom_2 (hex, n*v repeats v):
  //   0 10 35 25 32 32 58 48 52 52 78 68 72 72 98 88 92 92 8 8
  //   1010
  //   1011
endmodule
