// Logisim project Multiplicador.circ as structural Verilog: 1 circuit, main circuit main
module main (
  input  A3,
  input  A2,
  input  A1,
  input  A0,
  input  Inicio,
  input  B3,
  input  B2,
  input  B1,
  input  B0,
  input  in_10,
  output [7:0] out_11,
  output [7:0] out_12,
  output [7:0] out_13
);

  wire clock_1_out;
  wire [7:0] rom_1_data;
  wire [8:5] d_ff_1_q;

  ROM #(.addrWidth(9)) rom_1 (.addr({d_ff_1_q, Inicio, B3, B2, B1, B0}), .data(rom_1_data));  // open: sel
  Clock clock_1 (.out(clock_1_out));
  D_Flip_Flop d_ff_1 (.clk(clock_1_out), .D(rom_1_data[4]), .Q(d_ff_1_q[5]));  // open: Qn, preset, en, reset
  D_Flip_Flop d_ff_2 (.clk(clock_1_out), .D(rom_1_data[5]), .Q(d_ff_1_q[6]));  // open: Qn, preset, en, reset
  D_Flip_Flop d_ff_3 (.clk(clock_1_out), .D(rom_1_data[6]), .Q(d_ff_1_q[7]));  // open: Qn, preset, en, reset
  D_Flip_Flop d_ff_4 (.clk(clock_1_out), .D(rom_1_data[7]), .Q(d_ff_1_q[8]));  // open: Qn, preset, en, reset
  Shift_Register shift_register_1 (
    .shift(rom_1_data[1]), .in(in_10), .clk(clock_1_out), .load(rom_1_data[3]), .d0(A0), .q0(out_11[0]),
    .d1(A1), .q1(out_11[1]), .d2(A2), .q2(out_11[2]), .d3(A3), .q3(out_11[3]), .d4(1'b0), .q4(out_11[4]),
    .d5(1'b0), .q5(out_11[5]), .d6(1'b0), .q6(out_11[6]), .d7(1'b0), .q7(out_11[7]));  // open: out, clr
  Adder adder_1 (.a(out_11), .b(out_13), .out(out_12));  // open: cin, cout
  Register register_1 (.D(out_12), .Q(out_13), .clk(rom_1_data[0]), .clr(rom_1_data[2]));  // open: en

  // Notes on the sheet:
  //   contents of rom_1 (hex, n*v repeats v):
  //   16*0 16*1c 16*0 30 20 30 20 30 20 30 20 30 20 30 20 30 20 30 20 16*0 16*31 16*0 52 52 42 42 52 52 42
  //   42 52 52 42 42 52 52 42 42 16*0 16*51 16*0 4*72 4*62 4*72 4*62 16*0 16*71 16*0 8*92 8*82 16*0 16*91
  //   16*0 16*2
endmodule
