// Logisim project Nuevo intento semaforo.circ as structural Verilog: 1 circuit, main circuit main
module main (
  output out_1
);

  wire clock_1_out, Rubix, S1, S2, S3, shift_register_1_q0, shift_register_1_q1, shift_register_1_q2,
       shift_register_2_q0, shift_register_2_q1, shift_register_2_q2, shift_register_3_q0,
       shift_register_3_q1, shift_register_3_q2;
  wire [3:0] d_ff_1_q;
  wire [7:4] rom_1_data;

  Clock clock_1 (.out(clock_1_out));
  Shift_Register #(.length(4)) shift_register_1 (
    .shift(S1), .in(shift_register_1_q2), .clk(clock_1_out), .load(Rubix), .d0(1'b1),
    .q0(shift_register_1_q0), .d1(1'b0), .q1(shift_register_1_q1), .d2(1'b0), .q2(shift_register_1_q2));  // open: out, clr, d3, q3
  LED led_1 (.in(shift_register_1_q2));
  LED led_2 (.in(shift_register_1_q1));
  LED led_3 (.in(shift_register_1_q0));
  ROM #(.addrWidth(4)) rom_1 (.addr(d_ff_1_q), .data({rom_1_data, Rubix, S3, S2, S1}));  // open: sel
  D_Flip_Flop d_ff_1 (.clk(clock_1_out), .D(rom_1_data[4]), .Q(d_ff_1_q[0]));  // open: Qn, preset, en, reset
  D_Flip_Flop d_ff_2 (.clk(clock_1_out), .D(rom_1_data[5]), .Q(d_ff_1_q[1]));  // open: Qn, preset, en, reset
  LED led_4 (.in(shift_register_3_q2));
  LED led_5 (.in(shift_register_3_q1));
  LED led_6 (.in(shift_register_3_q0));
  D_Flip_Flop d_ff_3 (.clk(clock_1_out), .D(rom_1_data[6]), .Q(d_ff_1_q[2]));  // open: Qn, preset, en, reset
  Shift_Register #(.length(4)) shift_register_2 (
    .shift(S2), .in(shift_register_2_q2), .clk(clock_1_out), .load(Rubix), .d0(1'b1),
    .q0(shift_register_2_q0), .d1(1'b0), .q1(shift_register_2_q1), .d2(1'b0), .q2(shift_register_2_q2));  // open: out, clr, d3, q3
  Shift_Register #(.length(4)) shift_register_3 (
    .shift(S3), .in(shift_register_3_q2), .clk(clock_1_out), .load(Rubix), .d0(1'b1),
    .q0(shift_register_3_q0), .d1(1'b0), .q1(shift_register_3_q1), .d2(1'b0), .q2(shift_register_3_q2));  // open: out, clr, d3, q3
  // AND_Gate and_1 has open pins: out=out_1
  D_Flip_Flop d_ff_4 (.clk(clock_1_out), .D(rom_1_data[7]), .Q(d_ff_1_q[3]));  // open: Qn, preset, en, reset
  LED led_7 (.in(shift_register_2_q2));
  LED led_8 (.in(shift_register_2_q1));
  LED led_9 (.in(shift_register_2_q0));

  // Notes on the sheet:
  //   contents of rom_1 (hex, n*v repeats v):
  //   11 21 37 42 56 65
endmodule
