// Logisim project P1 (1).circ as structural Verilog: 2 circuits, main circuit main
module main (
  input  D,
  input  C,
  input  B,
  input  A,
  output D7,
  output P1,
  output D6,
  output P4,
  output D5,
  output P2,
  output D3
);

  wire and_1_out, and_2_out, and_3_out, and_4_out, and_5_out, and_6_out, not_1_out, not_2_out, not_4_out,
       or_2_out, xor_1_out, xor_3_out, xor_5_out;

  not not_1 (not_1_out, D);
  not not_2 (not_2_out, C);
  not not_3 (D5, B);
  not not_4 (not_4_out, A);
  and and_1 (and_1_out, not_1_out, not_2_out);
  and and_2 (and_2_out, D, B);
  and and_3 (and_3_out, not_2_out, D5);
  and and_4 (and_4_out, C, B);
  and and_5 (and_5_out, and_1_out, D5);
  or or_1 (D6, and_3_out, and_4_out);
  or or_2 (or_2_out, and_5_out, and_2_out);
  and and_6 (and_6_out, D, C);
  or or_3 (D7, or_2_out, and_6_out);
  xor xor_1 (xor_1_out, D5, A);
  xor xor_2 (P1, D7, xor_1_out);
  xor xor_3 (xor_3_out, D6, A);
  xor xor_4 (P2, D7, xor_3_out);
  xor xor_5 (xor_5_out, D6, D5);
  xor xor_6 (P4, D7, xor_5_out);

  assign D3 = A;
endmodule

module P1 (
  input  D,
  input  C,
  input  B,
  input  A,
  output P2
);

  wire and_1_out, and_2_out, and_3_out, and_4_out, and_5_out, and_6_out, and_7_out, and_8_out, not_1_out,
       not_2_out, not_3_out, not_4_out, not_5_out, not_6_out, not_7_out, or_1_out, or_2_out, or_3_out,
       or_4_out;

  not not_1 (not_1_out, C);
  or or_1 (or_1_out, not_1_out, B);
  or or_2 (or_2_out, B, not_2_out);
  not not_2 (not_2_out, C);
  not not_3 (not_3_out, A);
  and and_1 (and_1_out, not_3_out, not_4_out);
  not not_4 (not_4_out, D);
  and and_2 (and_2_out, A, D);
  and and_3 (and_3_out, D, or_1_out);
  not not_5 (not_5_out, A);
  and and_4 (and_4_out, A, or_2_out);
  not not_6 (not_6_out, D);
  or or_3 (or_3_out, and_1_out, and_2_out);
  and and_5 (and_5_out, and_3_out, not_5_out);
  and and_6 (and_6_out, and_4_out, not_6_out);
  and and_7 (and_7_out, C, or_3_out);
  not not_7 (not_7_out, B);
  or or_4 (or_4_out, and_5_out, and_6_out);
  and and_8 (and_8_out, and_7_out, not_7_out);
  or or_5 (P2, or_4_out, and_8_out);
endmodule
