// Logisim project P5.circ as structural Verilog: 1 circuit, main circuit main
module main (
  input  S0,
  input  S1,
  output X3,
  output X2,
  output X1,
  output X0
);

  wire clock_1_out;
  wire [3:0] ram_1_data;

  RAM #(.addrWidth(6), .dataWidth(4)) ram_1 (
    .addr({S0, S1, X0, X1, X2, X3}), .data(ram_1_data));  // open: sel, clk, ld, clr
  Clock clock_1 (.out(clock_1_out));
  D_Flip_Flop d_ff_1 (.clk(clock_1_out), .D(ram_1_data[3]), .Q(X3));  // open: Qn, preset, en, reset
  D_Flip_Flop d_ff_2 (.clk(clock_1_out), .D(ram_1_data[2]), .Q(X2));  // open: Qn, preset, en, reset
  D_Flip_Flop d_ff_3 (.clk(clock_1_out), .D(ram_1_data[1]), .Q(X1));  // open: Qn, preset, en, reset
  D_Flip_Flop d_ff_4 (.clk(clock_1_out), .D(ram_1_data[0]), .Q(X0));  // open: Qn, preset, en, reset

  // Other names for the same wires on the sheet: Q3 = X3; Q2 = X2; Q1 = X1; Q0 = X0

  // Notes on the sheet:
  //   Q = X
  //   X0
  //   X1
  //   X2
  //   X3
  //   Siguiente estado
  //   Y3
  //   Y0
  //   Y2
  //   Y1
  //   Estado actual
endmodule
