// Logisim project PRACTICA 1-FINAL.circ as structural Verilog: 1 circuit, main circuit main
module main (
  input  D,
  input  C,
  input  B,
  input  A
);

  wire and_1_out, and_2_out, and_3_out, and_4_out, and_5_out, and_6_out, and_7_out, not_1_out, not_2_out,
       not_3_out, not_4_out, or_1_out, or_2_out, or_3_out;

  not not_1 (not_1_out, D);
  not not_2 (not_2_out, C);
  not not_3 (not_3_out, B);
  not not_4 (not_4_out, A);
  and and_1 (and_1_out, not_1_out, A);
  and and_2 (and_2_out, not_1_out, not_2_out);
  and and_3 (and_3_out, not_2_out, B);
  and and_4 (and_4_out, C, not_3_out);
  and and_5 (and_5_out, and_2_out, B);
  and and_6 (and_6_out, and_3_out, A);
  or or_1 (or_1_out, and_1_out, and_5_out);
  and and_7 (and_7_out, and_4_out, A);
  or or_2 (or_2_out, and_6_out, and_7_out);
  or or_3 (or_3_out, or_1_out, or_2_out);
  LED led_1 (.in(or_3_out));

  // Notes on the sheet:
  //   ~DA
  //   ~D~C
  //   ~CB
  //   C~B
  //   ~D~CB
  //   ~CBA
  //   C~B(A)
  //   (~DA)+(~D~CB)
  //   (~CBA) + (C~BA)
  //   (~DA)+(~D~CB) + (~CBA) + (C~BA)
endmodule
