// Logisim project P2-CON-XOR.circ as structural Verilog: 1 circuit, main circuit main
module main (
  input  D,
  input  C,
  input  B,
  input  A
);

  wire and_1_out, and_2_out, and_3_out, and_4_out, and_5_out, and_6_out, and_7_out, and_8_out, and_9_out,
       and_10_out, and_11_out, and_12_out, and_13_out, and_14_out, and_15_out, and_16_out, and_17_out,
       and_18_out, and_19_out, and_20_out, not_1_out, not_2_out, not_3_out, not_4_out, or_1_out, or_2_out,
       or_3_out, or_4_out, or_5_out, or_6_out, or_7_out, or_8_out, or_9_out, xor_1_out, xor_2_out, xor_3_out,
       xor_4_out, xor_5_out, xor_6_out;

  not not_1 (not_1_out, D);
  not not_2 (not_2_out, C);
  not not_3 (not_3_out, B);
  not not_4 (not_4_out, A);
  and and_1 (and_1_out, not_1_out, not_3_out);
  and and_2 (and_2_out, D, B);
  and and_3 (and_3_out, not_3_out, not_4_out);
  and and_4 (and_4_out, B, A);
  xor xor_1 (xor_1_out, D, not_3_out);
  or or_1 (or_1_out, and_1_out, and_2_out);
  xor xor_2 (xor_2_out, D, A);
  or or_2 (or_2_out, and_3_out, and_4_out);
  and and_5 (and_5_out, D, C);
  xor xor_3 (xor_3_out, B, A);
  and and_6 (and_6_out, not_1_out, C);
  xor xor_4 (xor_4_out, D, A);
  and and_7 (and_7_out, not_3_out, not_4_out);
  and and_8 (and_8_out, B, A);
  and and_9 (and_9_out, not_1_out, C);
  xor xor_5 (xor_5_out, B, A);
  and and_10 (and_10_out, D, C);
  and and_11 (and_11_out, xor_1_out, not_2_out);
  and and_12 (and_12_out, D, C);
  and and_13 (and_13_out, or_1_out, not_2_out);
  and and_14 (and_14_out, C, not_1_out);
  and and_15 (and_15_out, xor_2_out, not_2_out);
  and and_16 (and_16_out, xor_3_out, and_6_out);
  and and_17 (and_17_out, xor_4_out, not_2_out);
  or or_3 (or_3_out, and_7_out, and_8_out);
  and and_18 (and_18_out, xor_5_out, and_10_out);
  or or_4 (or_4_out, and_15_out, and_16_out);
  and and_19 (and_19_out, or_2_out, and_5_out);
  and and_20 (and_20_out, or_3_out, and_9_out);
  LED led_1 (.in(or_5_out));
  or or_5 (or_5_out, and_11_out, and_12_out);
  xor xor_6 (xor_6_out, not_2_out, B);
  LED led_2 (.in(xor_6_out));
  LED led_3 (.in(not_3_out));
  or or_6 (or_6_out, and_13_out, and_14_out);
  LED led_4 (.in(or_6_out));
  LED led_5 (.in(A));
  or or_7 (or_7_out, or_4_out, and_19_out);
  or or_8 (or_8_out, and_17_out, and_20_out);
  LED led_6 (.in(or_7_out));
  or or_9 (or_9_out, or_8_out, and_18_out);
  LED led_7 (.in(or_9_out));
endmodule
