// Logisim project Práctica 3.circ as structural Verilog: 1 circuit, main circuit main
module main (
  input  D7,
  input  D6,
  input  D5,
  input  P4,
  input  D3,
  input  P2,
  input  P1,
  output D,
  output out_9,
  output C,
  output out_11,
  output out_12,
  output B,
  output A
);

  wire and_1_out, and_2_out, and_3_out, and_4_out, and_5_out, and_6_out, and_7_out, and_8_out, and_9_out,
       and_10_out, and_11_out, and_12_out, and_13_out, and_14_out, and_15_out, and_16_out, and_17_out,
       and_18_out, and_19_out, not_1_out, not_2_out, not_3_out, not_4_out, not_5_out, not_6_out, not_7_out,
       or_1_out, or_2_out, or_3_out, or_4_out, or_5_out, or_9_out, xor_1_out, xor_2_out, xor_3_out,
       xor_4_out, xor_5_out, xor_6_out, xor_7_out, xor_8_out, xor_9_out, xor_10_out, xor_11_out, xor_12_out,
       xor_13_out, xor_14_out, xor_15_out, xor_16_out;

  xor xor_1 (xor_1_out, P1, D3);
  xor xor_2 (xor_2_out, D5, D7);
  xor xor_3 (xor_3_out, P2, D3);
  xor xor_4 (xor_4_out, D6, D7);
  xor xor_5 (xor_5_out, P4, D5);
  xor xor_6 (xor_6_out, D6, D7);
  xor xor_7 (xor_7_out, xor_1_out, xor_2_out);
  xor xor_8 (xor_8_out, xor_3_out, xor_4_out);
  xor xor_9 (xor_9_out, xor_5_out, xor_6_out);
  not not_1 (not_1_out, xor_7_out);
  not not_2 (not_2_out, xor_8_out);
  not not_3 (not_3_out, xor_9_out);
  and and_1 (and_1_out, not_3_out, xor_8_out);
  and and_2 (and_2_out, and_1_out, xor_10_out);
  xor xor_10 (xor_10_out, D3, xor_7_out);
  and and_3 (and_3_out, D3, or_1_out);
  or or_1 (or_1_out, xor_9_out, not_2_out);
  and and_4 (and_4_out, not_2_out, xor_7_out);
  and and_5 (and_5_out, and_4_out, xor_11_out);
  xor xor_11 (xor_11_out, D5, xor_9_out);
  and and_6 (and_6_out, D5, or_2_out);
  or or_2 (or_2_out, not_1_out, xor_8_out);
  and and_7 (and_7_out, xor_9_out, xor_8_out);
  xor xor_12 (xor_12_out, D7, xor_7_out);
  or or_3 (or_3_out, not_3_out, not_2_out);
  and and_8 (and_8_out, D6, or_4_out);
  or or_4 (or_4_out, not_2_out, not_3_out);
  and and_9 (and_9_out, xor_9_out, xor_8_out);
  not not_4 (not_4_out, xor_13_out);
  xor xor_13 (xor_13_out, D6, xor_7_out);
  or or_5 (or_5_out, and_2_out, and_3_out);
  or or_6 (out_9, and_5_out, and_6_out);
  and and_10 (and_10_out, and_7_out, xor_12_out);
  and and_11 (and_11_out, D7, or_3_out);
  and and_12 (and_12_out, and_9_out, not_4_out);
  or or_7 (out_11, and_10_out, and_11_out);
  or or_8 (out_12, and_8_out, and_12_out);
  not not_5 (not_5_out, out_11);
  not not_6 (not_6_out, out_12);
  not not_7 (not_7_out, out_9);
  not not_8 (A, or_5_out);
  and and_13 (and_13_out, not_5_out, out_12);
  and and_14 (and_14_out, out_12, A);
  xor xor_14 (xor_14_out, out_11, out_9);
  xor xor_15 (xor_15_out, out_12, or_5_out);
  xor xor_16 (xor_16_out, out_9, or_5_out);
  and and_15 (and_15_out, or_5_out, and_13_out);
  and and_16 (and_16_out, out_11, not_6_out);
  and and_17 (and_17_out, and_14_out, xor_14_out);
  and and_18 (and_18_out, not_7_out, xor_15_out);
  and and_19 (and_19_out, not_6_out, out_9);
  not not_9 (B, xor_16_out);
  or or_9 (or_9_out, and_15_out, and_16_out);
  or or_10 (C, and_18_out, and_19_out);
  or or_11 (D, or_9_out, and_17_out);

  // Notes on the sheet:
  //   C1
  //   C2
  //   C4
  //   C1
  //   C2
  //   C4
  //   D3c
  //   D5c
  //   D7c
  //   D6c
  //   D7
  //   D6
  //   D5
  //   D3
endmodule
