// Logisim project SEMAFORO22 - copia.circ as structural Verilog: 1 circuit, main circuit main
module main (
);

  wire and_1_out, CLK, S00, S01, S02, S11, shift_register_1_out, shift_register_1_q0, shift_register_1_q1,
       shift_register_1_q2, shift_register_2_out, shift_register_2_q0, shift_register_2_q1,
       shift_register_3_out, shift_register_3_q0, shift_register_3_q1;
  wire [3:0] d_ff_1_q;
  wire [7:4] rom_1_data;

  ROM #(.addrWidth(4)) rom_1 (.addr(d_ff_1_q), .data({rom_1_data, S11, S02, S01, S00}));
  D_Flip_Flop d_ff_1 (.D(rom_1_data[4]), .clk(CLK), .Q(d_ff_1_q[0]));  // open: Qn, preset, reset
  D_Flip_Flop d_ff_2 (.D(rom_1_data[5]), .clk(CLK), .Q(d_ff_1_q[1]));  // open: Qn, preset, reset
  D_Flip_Flop d_ff_3 (.D(rom_1_data[6]), .clk(CLK), .Q(d_ff_1_q[2]));  // open: Qn, preset, reset
  D_Flip_Flop d_ff_4 (.D(rom_1_data[7]), .clk(CLK), .Q(d_ff_1_q[3]));  // open: Qn, preset, reset
  Clock clock_1 (.out(CLK));
  LED led_1 (.in(shift_register_1_q2));
  LED led_2 (.in(shift_register_1_q1));
  LED led_3 (.in(shift_register_1_q0));
  LED led_4 (.in(shift_register_2_out));
  LED led_5 (.in(shift_register_2_q1));
  LED led_6 (.in(shift_register_2_q0));
  LED led_7 (.in(shift_register_3_q0));
  Shift_Register #(.length(4)) shift_register_1 (
    .shift(S00), .in(shift_register_1_q2), .clk(CLK), .out(shift_register_1_out), .load(S11), .d0(1'b1),
    .q0(shift_register_1_q0), .d1(1'b0), .q1(shift_register_1_q1), .d2(1'b0), .q2(shift_register_1_q2),
    .d3(1'b0));  // open: clr, q3
  LED led_8 (.in(shift_register_3_out));
  LED led_9 (.in(shift_register_3_q1));
  Shift_Register #(.length(3)) shift_register_2 (
    .shift(S01), .in(shift_register_2_out), .clk(CLK), .out(shift_register_2_out), .load(S11), .d0(1'b1),
    .q0(shift_register_2_q0), .d1(1'b0), .q1(shift_register_2_q1), .d2(1'b0));  // open: clr, q2
  Shift_Register #(.length(3)) shift_register_3 (
    .shift(S02), .in(shift_register_3_out), .clk(CLK), .out(shift_register_3_out), .load(S11), .d0(1'b1),
    .q0(shift_register_3_q0), .d1(1'b0), .q1(shift_register_3_q1), .d2(1'b0));  // open: clr, q2
  and and_1 (and_1_out, shift_register_2_q0, shift_register_3_q1);
  LED led_10 (.in(and_1_out));

  // Notes on the sheet:
  //   contents of rom_1 (hex, n*v repeats v):
  //   19 21 30 40 50 67 72 80 90 a0 b2 c4 d0 e0 f0 15
endmodule
