// Logisim project elevador.circ as structural Verilog: 1 circuit, main circuit main
module main (
  input  S_B,
  input  mover,
  input  borrarS,
  input  borrarB,
  output BSubida,
  output subir,
  output [1:0] PS,
  output out_8,
  output bajar,
  output out_10,
  output subir_2,
  output out_12,
  output bajar_2,
  output [1:0] PB
);

  wire button_1_out, button_2_out, button_3_out, button_4_out, button_5_out, button_6_out, clock, d_ff_1_q,
       d_ff_2_q, d_ff_3_q, d_ff_4_q, d_ff_5_q, d_ff_6_q, decoder_1_out0, decoder_1_out1, decoder_1_out2,
       decoder_2_out0, decoder_2_out1, decoder_2_out2, multiplexer_1_out, multiplexer_2_out, not_1_out,
       not_2_out;
  wire [1:0] PisoActual;
  wire [3:2] counter_3_q;

  Button button_1 (.out(button_1_out));
  Button button_2 (.out(button_2_out));
  Button button_3 (.out(button_3_out));
  Decoder #(.select(2)) decoder_1 (
    .out0(decoder_1_out0), .out1(decoder_1_out1), .out2(decoder_1_out2), .sel(PisoActual), .en(borrarS));  // open: out3
  Button button_4 (.out(button_4_out));
  Button button_5 (.out(button_5_out));
  Button button_6 (.out(button_6_out));
  Decoder #(.select(2)) decoder_2 (
    .out0(decoder_2_out0), .out1(decoder_2_out1), .out2(decoder_2_out2), .sel(PisoActual), .en(borrarB));  // open: out3
  D_Flip_Flop d_ff_1 (.D(1'b1), .clk(button_1_out), .Q(d_ff_1_q), .reset(decoder_1_out0));  // open: Qn, preset
  D_Flip_Flop d_ff_2 (.D(1'b1), .clk(button_2_out), .Q(d_ff_2_q), .reset(decoder_1_out1));  // open: Qn, preset
  D_Flip_Flop d_ff_3 (.D(1'b1), .clk(button_3_out), .Q(d_ff_3_q), .reset(decoder_1_out2));  // open: Qn, preset
  D_Flip_Flop d_ff_4 (.D(1'b1), .clk(button_4_out), .Q(d_ff_4_q), .reset(decoder_2_out0));  // open: Qn, preset
  D_Flip_Flop d_ff_5 (.D(1'b1), .clk(button_5_out), .Q(d_ff_5_q), .reset(decoder_2_out1));  // open: Qn, preset
  D_Flip_Flop d_ff_6 (.D(1'b1), .clk(button_6_out), .Q(d_ff_6_q), .reset(decoder_2_out2));  // open: Qn, preset
  Counter #(.max('h3), .width(2)) counter_1 (
    .load(1'b0), .up(1'b1), .count(not_1_out), .clk(clock), .Q(PS));  // open: clr, D, carry
  Counter #(.max('h3), .width(2)) counter_2 (
    .load(1'b0), .up(1'b1), .count(not_2_out), .clk(clock), .Q(PB));  // open: clr, D, carry
  Multiplexer #(.select(2)) multiplexer_1 (
    .in0(1'b0), .in1(d_ff_4_q), .in2(d_ff_5_q), .in3(d_ff_6_q), .out(multiplexer_1_out), .sel(PB));
  not not_1 (not_1_out, multiplexer_2_out);
  Multiplexer #(.select(2)) multiplexer_2 (
    .in0(d_ff_1_q), .in1(d_ff_2_q), .in2(d_ff_3_q), .in3(1'b0), .out(multiplexer_2_out), .sel(PS));
  not not_2 (not_2_out, multiplexer_1_out);
  or or_1 (BSubida, d_ff_1_q, d_ff_2_q, d_ff_3_q);
  or or_2 (out_10, d_ff_4_q, d_ff_5_q, d_ff_6_q);
  Clock clock_1 (.out(clock));
  Counter #(.max('hf), .width(4)) counter_3 (
    .load(1'b0), .up(S_B), .count(mover), .clk(clock), .Q({counter_3_q, PisoActual}));  // open: clr, D, carry
  Comparator #(.width(2)) comparator_1 (.a(PisoActual), .b(PS), .gt(subir), .eq(out_8), .lt(bajar));
  Comparator #(.width(2)) comparator_2 (.a(PisoActual), .b(PB), .gt(subir_2), .eq(out_12), .lt(bajar_2));
  Hex_Digit_Display hex_digit_display_1 (.value({2'b00, PisoActual}));  // open: dp

  // Notes on the sheet:
  //   B1B
  //   B2B
  //   B3B
  //   B0S
  //   B1S
  //   B2S
  //   llamada subir
  //   llamada subir
  //   Bbajada
  //   ELEVADOR
  //   llego al piso
  //   llego al piso
endmodule
